// Logisim project ProjCPU.circ as structural Verilog: 6 circuits, main circuit regfile
module CPUmain (
);

  wire alu_1_branch, control_1_from_mem, control_1_imm_sel, control_1_j, control_1_jr, control_1_mem_w_e,
       control_1_reg_write_e, or_1_out;
  wire [3:0] control_1_alu_code;
  wire [4:0] control_1_rd, control_1_rs, control_1_rt;
  wire [15:0] bit_extender_1_out;
  wire [31:0] adder_1_out, adder_2_out, alu_1_res, control_1_imm, mem_1_data_out, multiplexer_1_out,
       multiplexer_2_out, multiplexer_3_out, multiplexer_4_out, multiplexer_5_out, multiplexer_6_out, PC_q,
       regfile_1_rs_data, regfile_1_rt_data, romu_1_out_2, shifter_1_out;

  Adder #(.width(32)) adder_1 (.a(PC_q), .b(32'h4), .out(adder_1_out));  // open: cin, cout
  Adder #(.width(32)) adder_2 (.a(adder_1_out), .b(control_1_imm), .out(adder_2_out));  // open: cin, cout
  Multiplexer #(.width(32)) multiplexer_1 (
    .in0(adder_1_out), .in1(adder_2_out), .out(multiplexer_1_out), .sel(alu_1_branch));
  Multiplexer #(.width(32)) multiplexer_2 (
    .in0(regfile_1_rs_data), .in1(romu_1_out_2), .out(multiplexer_2_out), .sel(control_1_j));
  Multiplexer #(.width(32)) multiplexer_3 (
    .in0(multiplexer_1_out), .in1(multiplexer_2_out), .out(multiplexer_3_out), .sel(or_1_out));
  Register #(.width(32)) PC (.D(multiplexer_3_out), .en(1'b1), .Q(PC_q));  // open: clk, clr
  Clock clock_1 ();  // open: out
  Shifter #(.shift("lr"), .width(32)) shifter_1 (.in(PC_q), .\dist (5'b00010), .out(shifter_1_out));
  Bit_Extender #(.in_width(32)) bit_extender_1 (.in(shifter_1_out), .out(bit_extender_1_out));
  ROMu romu_1 (.in_1(bit_extender_1_out), .out_2(romu_1_out_2));
  Multiplexer #(.width(32)) multiplexer_4 (
    .in0(adder_1_out), .in1(multiplexer_6_out), .out(multiplexer_4_out), .sel(or_1_out));
  or or_1 (or_1_out, control_1_j, control_1_jr);
  regfile regfile_1 (
    .rd(control_1_rd), .w_e(control_1_reg_write_e), .rt(control_1_rt), .rd_data(multiplexer_4_out),
    .rs(control_1_rs), .rs_data(regfile_1_rs_data), .rt_data(regfile_1_rt_data));
  Control control_1 (
    .Inst(romu_1_out_2), .ALU_code(control_1_alu_code), .rs(control_1_rs), .rt(control_1_rt),
    .rd(control_1_rd), .imm_sel(control_1_imm_sel), .from_mem(control_1_from_mem), .j(control_1_j),
    .jr(control_1_jr), .mem_w_e(control_1_mem_w_e), .reg_write_e(control_1_reg_write_e), .imm(control_1_imm));
  Multiplexer #(.width(32)) multiplexer_5 (
    .in0(regfile_1_rt_data), .in1(control_1_imm), .out(multiplexer_5_out), .sel(control_1_imm_sel));
  Multiplexer #(.width(32)) multiplexer_6 (
    .in0(alu_1_res), .in1(mem_1_data_out), .out(multiplexer_6_out), .sel(control_1_from_mem));
  ALU alu_1 (
    .OP2(multiplexer_5_out), .OP1(regfile_1_rs_data), .ALU_CODE(control_1_alu_code), .Res(alu_1_res),
    .Branch(alu_1_branch));
  MEM mem_1 (.add(alu_1_res), .data_in(control_1_imm), .in_2(control_1_mem_w_e), .data_out(mem_1_data_out));
endmodule

module regfile (
  input  [31:0] rd_data,
  input  w_e,
  input  [4:0] rd,
  input  [4:0] rt,
  input  [4:0] rs,
  output [31:0] rt_data,
  output [31:0] rs_data
);

  wire clock_1_out, clock_2_out, clock_3_out, clock_4_out, clock_5_out, clock_6_out, clock_7_out,
       clock_8_out, clock_9_out, clock_10_out, clock_11_out, clock_12_out, clock_13_out, clock_14_out,
       clock_15_out, clock_16_out, clock_17_out, clock_18_out, clock_19_out, clock_20_out, clock_21_out,
       clock_22_out, clock_23_out, clock_24_out, clock_25_out, clock_26_out, clock_27_out, clock_28_out,
       clock_29_out, clock_30_out, clock_31_out, demultiplexer_1_out1, demultiplexer_1_out2,
       demultiplexer_1_out3, demultiplexer_1_out4, demultiplexer_1_out5, demultiplexer_1_out6,
       demultiplexer_1_out7, demultiplexer_1_out8, demultiplexer_1_out9, demultiplexer_1_out10,
       demultiplexer_1_out11, demultiplexer_1_out12, demultiplexer_1_out13, demultiplexer_1_out14,
       demultiplexer_1_out15, demultiplexer_1_out16, demultiplexer_1_out17, demultiplexer_1_out18,
       demultiplexer_1_out19, demultiplexer_1_out20, demultiplexer_1_out21, demultiplexer_1_out22,
       demultiplexer_1_out23, demultiplexer_1_out24, demultiplexer_1_out25, demultiplexer_1_out26,
       demultiplexer_1_out27, demultiplexer_1_out28, demultiplexer_1_out29, demultiplexer_1_out30,
       demultiplexer_1_out31;
  wire [31:0] aone_q, at_q, athree_q, atwo_q, azero_q, fp_q, gp_q, kone_q, kzero_q, ra_q, sfive_q, sfour_q,
       sone_q, sp_q, sseven_q, ssix_q, sthree_q, stwo_q, szero_q, teight_q, tfive_q, tfour_q, tnine_q,
       tone_q, tseven_q, tsix_q, tthree_q, ttwo_q, tzero_q, vone_q, vzero_q;

  Register #(.width(32)) at (.D(rd_data), .en(demultiplexer_1_out1), .clk(clock_1_out), .Q(at_q));  // open: clr
  Clock clock_1 (.out(clock_1_out));
  Register #(.width(32)) vzero (.D(rd_data), .en(demultiplexer_1_out2), .clk(clock_2_out), .Q(vzero_q));  // open: clr
  Clock clock_2 (.out(clock_2_out));
  Register #(.width(32)) vone (.D(rd_data), .en(demultiplexer_1_out3), .clk(clock_3_out), .Q(vone_q));  // open: clr
  Clock clock_3 (.out(clock_3_out));
  Register #(.width(32)) azero (.D(rd_data), .en(demultiplexer_1_out4), .clk(clock_4_out), .Q(azero_q));  // open: clr
  Clock clock_4 (.out(clock_4_out));
  Register #(.width(32)) aone (.D(rd_data), .en(demultiplexer_1_out5), .clk(clock_5_out), .Q(aone_q));  // open: clr
  Clock clock_5 (.out(clock_5_out));
  Register #(.width(32)) atwo (.D(rd_data), .en(demultiplexer_1_out6), .clk(clock_6_out), .Q(atwo_q));  // open: clr
  Clock clock_6 (.out(clock_6_out));
  Register #(.width(32)) athree (.D(rd_data), .en(demultiplexer_1_out7), .clk(clock_7_out), .Q(athree_q));  // open: clr
  Clock clock_7 (.out(clock_7_out));
  Register #(.width(32)) tzero (.D(rd_data), .en(demultiplexer_1_out8), .clk(clock_8_out), .Q(tzero_q));  // open: clr
  Clock clock_8 (.out(clock_8_out));
  Register #(.width(32)) tone (.D(rd_data), .en(demultiplexer_1_out9), .clk(clock_9_out), .Q(tone_q));  // open: clr
  Clock clock_9 (.out(clock_9_out));
  Register #(.width(32)) ttwo (.D(rd_data), .en(demultiplexer_1_out10), .clk(clock_10_out), .Q(ttwo_q));  // open: clr
  Clock clock_10 (.out(clock_10_out));
  Register #(.width(32)) tthree (
    .D(rd_data), .en(demultiplexer_1_out11), .clk(clock_11_out), .Q(tthree_q));  // open: clr
  Clock clock_11 (.out(clock_11_out));
  Register #(.width(32)) tfour (.D(rd_data), .en(demultiplexer_1_out12), .clk(clock_12_out), .Q(tfour_q));  // open: clr
  Clock clock_12 (.out(clock_12_out));
  Multiplexer #(.select(5), .width(32)) multiplexer_1 (
    .in0({32{1'b0}}), .in1(at_q), .in2(vzero_q), .in3(vone_q), .in4(azero_q), .in5(aone_q), .in6(atwo_q),
    .in7(athree_q), .in8(tzero_q), .in9(tone_q), .in10(ttwo_q), .in11(tthree_q), .in12(tfour_q),
    .in13(tfive_q), .in14(tsix_q), .in15(tseven_q), .in16(szero_q), .in17(sone_q), .in18(stwo_q),
    .in19(sthree_q), .in20(sfour_q), .in21(sfive_q), .in22(ssix_q), .in23(sseven_q), .in24(teight_q),
    .in25(tnine_q), .in26(kzero_q), .in27(kone_q), .in28(gp_q), .in29(sp_q), .in30(fp_q), .in31(ra_q),
    .out(rs_data), .sel(rs));
  Register #(.width(32)) tfive (.D(rd_data), .en(demultiplexer_1_out13), .clk(clock_13_out), .Q(tfive_q));  // open: clr
  Clock clock_13 (.out(clock_13_out));
  Register #(.width(32)) tsix (.D(rd_data), .en(demultiplexer_1_out14), .clk(clock_14_out), .Q(tsix_q));  // open: clr
  Clock clock_14 (.out(clock_14_out));
  Register #(.width(32)) tseven (
    .D(rd_data), .en(demultiplexer_1_out15), .clk(clock_15_out), .Q(tseven_q));  // open: clr
  Clock clock_15 (.out(clock_15_out));
  Register #(.width(32)) szero (.D(rd_data), .en(demultiplexer_1_out16), .clk(clock_16_out), .Q(szero_q));  // open: clr
  Clock clock_16 (.out(clock_16_out));
  Demultiplexer #(.select(5)) demultiplexer_1 (
    .out1(demultiplexer_1_out1), .out2(demultiplexer_1_out2), .out3(demultiplexer_1_out3),
    .out4(demultiplexer_1_out4), .out5(demultiplexer_1_out5), .out6(demultiplexer_1_out6),
    .out7(demultiplexer_1_out7), .out8(demultiplexer_1_out8), .out9(demultiplexer_1_out9),
    .out10(demultiplexer_1_out10), .out11(demultiplexer_1_out11), .out12(demultiplexer_1_out12),
    .out13(demultiplexer_1_out13), .out14(demultiplexer_1_out14), .out15(demultiplexer_1_out15),
    .out16(demultiplexer_1_out16), .out17(demultiplexer_1_out17), .out18(demultiplexer_1_out18),
    .out19(demultiplexer_1_out19), .out20(demultiplexer_1_out20), .out21(demultiplexer_1_out21),
    .out22(demultiplexer_1_out22), .out23(demultiplexer_1_out23), .out24(demultiplexer_1_out24),
    .out25(demultiplexer_1_out25), .out26(demultiplexer_1_out26), .out27(demultiplexer_1_out27),
    .out28(demultiplexer_1_out28), .out29(demultiplexer_1_out29), .out30(demultiplexer_1_out30),
    .out31(demultiplexer_1_out31), .in(w_e), .sel(rd));  // open: out0
  Register #(.width(32)) sone (.D(rd_data), .en(demultiplexer_1_out17), .clk(clock_17_out), .Q(sone_q));  // open: clr
  Clock clock_17 (.out(clock_17_out));
  Register #(.width(32)) stwo (.D(rd_data), .en(demultiplexer_1_out18), .clk(clock_18_out), .Q(stwo_q));  // open: clr
  Clock clock_18 (.out(clock_18_out));
  Register #(.width(32)) sthree (
    .D(rd_data), .en(demultiplexer_1_out19), .clk(clock_19_out), .Q(sthree_q));  // open: clr
  Clock clock_19 (.out(clock_19_out));
  Register #(.width(32)) sfour (.D(rd_data), .en(demultiplexer_1_out20), .clk(clock_20_out), .Q(sfour_q));  // open: clr
  Clock clock_20 (.out(clock_20_out));
  Register #(.width(32)) sfive (.D(rd_data), .en(demultiplexer_1_out21), .clk(clock_21_out), .Q(sfive_q));  // open: clr
  Clock clock_21 (.out(clock_21_out));
  Register #(.width(32)) ssix (.D(rd_data), .en(demultiplexer_1_out22), .clk(clock_22_out), .Q(ssix_q));  // open: clr
  Clock clock_22 (.out(clock_22_out));
  Register #(.width(32)) sseven (
    .D(rd_data), .en(demultiplexer_1_out23), .clk(clock_23_out), .Q(sseven_q));  // open: clr
  Clock clock_23 (.out(clock_23_out));
  Register #(.width(32)) teight (
    .D(rd_data), .en(demultiplexer_1_out24), .clk(clock_24_out), .Q(teight_q));  // open: clr
  Clock clock_24 (.out(clock_24_out));
  Multiplexer #(.select(5), .width(32)) multiplexer_2 (
    .in0({32{1'b0}}), .in1(at_q), .in2(vzero_q), .in3(vone_q), .in4(azero_q), .in5(aone_q), .in6(atwo_q),
    .in7(athree_q), .in8(tzero_q), .in9(tone_q), .in10(ttwo_q), .in11(tthree_q), .in12(tfour_q),
    .in13(tfive_q), .in14(tsix_q), .in15(tseven_q), .in16(szero_q), .in17(sone_q), .in18(stwo_q),
    .in19(sthree_q), .in20(sfour_q), .in21(sfive_q), .in22(ssix_q), .in23(sseven_q), .in24(teight_q),
    .in25(tnine_q), .in26(kzero_q), .in27(kone_q), .in28(gp_q), .in29(sp_q), .in30(fp_q), .out(rt_data),
    .sel(rt));  // open: in31
  Register #(.width(32)) tnine (.D(rd_data), .en(demultiplexer_1_out25), .clk(clock_25_out), .Q(tnine_q));  // open: clr
  Clock clock_25 (.out(clock_25_out));
  Register #(.width(32)) kzero (.D(rd_data), .en(demultiplexer_1_out26), .clk(clock_26_out), .Q(kzero_q));  // open: clr
  Clock clock_26 (.out(clock_26_out));
  Register #(.width(32)) kone (.D(rd_data), .en(demultiplexer_1_out27), .clk(clock_27_out), .Q(kone_q));  // open: clr
  Clock clock_27 (.out(clock_27_out));
  Register #(.width(32)) gp (.D(rd_data), .en(demultiplexer_1_out28), .clk(clock_28_out), .Q(gp_q));  // open: clr
  Clock clock_28 (.out(clock_28_out));
  Register #(.width(32)) sp (.D(rd_data), .en(demultiplexer_1_out29), .clk(clock_29_out), .Q(sp_q));  // open: clr
  Clock clock_29 (.out(clock_29_out));
  Register #(.width(32)) fp (.D(rd_data), .en(demultiplexer_1_out30), .clk(clock_30_out), .Q(fp_q));  // open: clr
  Clock clock_30 (.out(clock_30_out));
  Register #(.width(32)) ra (.D(rd_data), .en(demultiplexer_1_out31), .clk(clock_31_out), .Q(ra_q));  // open: clr
  Clock clock_31 (.out(clock_31_out));
endmodule

module ALU (
  input  [3:0] ALU_CODE,
  input  [31:0] OP1,
  input  [31:0] OP2,
  output [31:0] Res,
  output Branch
);

  wire and_1_out, clock_1_out, clock_2_out, comparator_1_eq, comparator_1_lt, not_1_out;
  wire [4:0] bit_extender_1_out;
  wire [31:0] adder_1_out, bit_extender_2_out, divider_1_out, divider_1_rem, HI_q, LO_q, multiplexer_1_out,
       multiplexer_2_out, multiplier_1_cout, multiplier_1_out, shifter_1_out, shifter_2_out, subtractor_1_out;

  Bit_Extender #(.in_width(32), .out_width(5)) bit_extender_1 (.in(OP2), .out(bit_extender_1_out));
  Adder #(.width(32)) adder_1 (.a(OP1), .b(OP2), .out(adder_1_out));  // open: cin, cout
  Subtractor #(.width(32)) subtractor_1 (.a(OP1), .b(OP2), .out(subtractor_1_out));  // open: bin, bout
  Multiplier #(.width(32)) multiplier_1 (
    .a(OP1), .b(OP2), .out(multiplier_1_out), .cout(multiplier_1_cout));  // open: cin
  Divider #(.width(32)) divider_1 (.a(OP1), .b(OP2), .out(divider_1_out), .rem(divider_1_rem));  // open: upper
  Comparator #(.width(32)) comparator_1 (.a(OP1), .b(OP2), .eq(comparator_1_eq), .lt(comparator_1_lt));  // open: gt
  Shifter #(.width(32)) shifter_1 (.in(OP1), .\dist (bit_extender_1_out), .out(shifter_1_out));
  Shifter #(.shift("lr"), .width(32)) shifter_2 (.in(OP1), .\dist (bit_extender_1_out), .out(shifter_2_out));
  assign bit_extender_2_out = {{31{1'b0}}, comparator_1_lt};  // Bit_Extender bit_extender_2
  Multiplexer #(.width(32)) multiplexer_1 (
    .in0(multiplier_1_cout), .in1(divider_1_rem), .out(multiplexer_1_out), .sel(ALU_CODE[0]));
  Multiplexer #(.width(32)) multiplexer_2 (
    .in0(multiplier_1_out), .in1(divider_1_out), .out(multiplexer_2_out), .sel(ALU_CODE[0]));
  and and_1 (and_1_out, ~ALU_CODE[2], ALU_CODE[1]);  // AND_Gate
  Register #(.width(32)) HI (.D(multiplexer_1_out), .en(and_1_out), .clk(clock_1_out), .Q(HI_q));  // open: clr
  Clock clock_1 (.out(clock_1_out));
  Register #(.width(32)) LO (.D(multiplexer_2_out), .en(and_1_out), .clk(clock_2_out), .Q(LO_q));  // open: clr
  Clock clock_2 (.out(clock_2_out));
  not not_1 (not_1_out, comparator_1_eq);
  Multiplexer #(.select(4), .width(32)) multiplexer_3 (
    .in0(adder_1_out), .in1(subtractor_1_out), .in2(multiplier_1_out), .in3(divider_1_out),
    .in4(bit_extender_2_out), .in5(shifter_1_out), .in6(shifter_2_out), .in8(HI_q), .in9(LO_q), .out(Res),
    .sel(ALU_CODE));  // open: in7, in10, in11, in12, in13, in14, in15
  Multiplexer multiplexer_4 (.in0(comparator_1_eq), .in1(not_1_out), .out(Branch), .sel(ALU_CODE[0]));
endmodule

module Control (
  input  [31:0] Inst,
  output from_mem,
  output j,
  output jr,
  output mem_w_e,
  output [4:0] rs,
  output [4:0] rt,
  output [4:0] rd,
  output [31:0] imm,
  output reg_write_e,
  output imm_sel,
  output [3:0] ALU_code
);

  wire and_1_out, and_2_out, and_3_out, and_4_out, and_5_out, and_6_out, and_7_out, and_8_out, and_9_out,
       comparator_1_eq, comparator_2_eq, comparator_3_eq, comparator_4_eq, comparator_5_eq, comparator_6_eq,
       comparator_7_eq, comparator_8_eq, comparator_9_eq, comparator_10_eq, comparator_11_eq;
  wire [15:0] bit_extender_1_out, multiplexer_2_out;

  Comparator #(.mode("unsigned"), .width(6)) comparator_1 (
    .a(Inst[31:26]), .b({6{1'b0}}), .eq(comparator_1_eq));  // open: gt, lt
  Comparator #(.mode("unsigned"), .width(6)) comparator_2 (
    .a(Inst[5:0]), .b(6'b011000), .eq(comparator_2_eq));  // open: gt, lt
  Comparator #(.mode("unsigned"), .width(6)) comparator_3 (
    .a(Inst[5:0]), .b(6'b010010), .eq(comparator_3_eq));  // open: gt, lt
  Comparator #(.mode("unsigned"), .width(6)) comparator_4 (
    .a(Inst[5:0]), .b(6'b010000), .eq(comparator_4_eq));  // open: gt, lt
  Comparator #(.mode("unsigned"), .width(6)) comparator_5 (
    .a(Inst[5:0]), .b({6{1'b0}}), .eq(comparator_5_eq));  // open: gt, lt
  Comparator #(.mode("unsigned"), .width(6)) comparator_6 (
    .a(Inst[5:0]), .b(6'b000010), .eq(comparator_6_eq));  // open: gt, lt
  Comparator #(.mode("unsigned"), .width(6)) comparator_7 (
    .a(Inst[5:0]), .b(6'b101010), .eq(comparator_7_eq));  // open: gt, lt
  Comparator #(.mode("unsigned"), .width(6)) comparator_8 (
    .a(Inst[31:26]), .b(6'b001000), .eq(comparator_8_eq));  // open: gt, lt
  Comparator #(.mode("unsigned"), .width(6)) comparator_9 (
    .a(Inst[5:0]), .b(6'b100000), .eq(comparator_9_eq));  // open: gt, lt
  Comparator #(.mode("unsigned"), .width(6)) comparator_10 (
    .a(Inst[5:0]), .b(6'b100010), .eq(comparator_10_eq));  // open: gt, lt
  Comparator #(.mode("unsigned"), .width(6)) comparator_11 (
    .a(Inst[5:0]), .b(6'b011010), .eq(comparator_11_eq));  // open: gt, lt
  and and_1 (and_1_out, comparator_1_eq, comparator_9_eq);
  and and_2 (and_2_out, comparator_1_eq, comparator_10_eq);
  and and_3 (and_3_out, comparator_1_eq, comparator_2_eq);
  and and_4 (and_4_out, comparator_1_eq, comparator_11_eq);
  and and_5 (and_5_out, comparator_1_eq, comparator_3_eq);
  and and_6 (and_6_out, comparator_1_eq, comparator_4_eq);
  and and_7 (and_7_out, comparator_1_eq, comparator_5_eq);
  and and_8 (and_8_out, comparator_1_eq, comparator_6_eq);
  and and_9 (and_9_out, comparator_1_eq, comparator_7_eq);
  or or_1 (ALU_code[0], and_2_out, and_4_out, and_5_out, and_7_out);
  or or_2 (ALU_code[1], and_3_out, and_4_out, and_8_out);
  or or_3 (ALU_code[2], and_7_out, and_8_out, and_9_out);
  Multiplexer #(.width(5)) multiplexer_1 (.in0(Inst[15:11]), .in1(Inst[20:16]), .out(rd), .sel(comparator_8_eq));
  or or_4 (ALU_code[3], and_5_out, and_6_out);
  or or_5 (reg_write_e, and_1_out, and_2_out, and_9_out, comparator_8_eq, and_8_out, and_7_out, comparator_8_eq);
  or or_6 (imm_sel, and_7_out, and_8_out, comparator_8_eq);
  assign bit_extender_1_out = {{11{1'b0}}, Inst[10:6]};  // Bit_Extender bit_extender_1
  Multiplexer #(.width(16)) multiplexer_2 (
    .in0(bit_extender_1_out), .in1(Inst[15:0]), .out(multiplexer_2_out), .sel(comparator_8_eq));
  assign imm = {{16{1'b0}}, multiplexer_2_out};  // Bit_Extender bit_extender_2

  assign rs = Inst[25:21];
  assign rt = Inst[20:16];

  // Notes on the sheet:
  //   i or j-types
  //   add
  //   sub
  //   mult
  //   div
  //   mflo
  //   mfhi
  //   sll
  //   srl
  //   slt
  //   addi
endmodule

module MEM (
  input  [31:0] add,
  input  in_2,
  input  [31:0] data_in,
  output [31:0] data_out
);

  wire clock_1_out;
  wire [15:0] bit_extender_1_out, shifter_1_out;

  Bit_Extender #(.in_width(32)) bit_extender_1 (.in(add), .out(bit_extender_1_out));
  Shifter #(.width(16)) shifter_1 (.in(bit_extender_1_out), .\dist (4'b0010), .out(shifter_1_out));
  RAM #(.addrWidth(16), .dataWidth(32), .enables("line")) ram_1 (
    .addr(shifter_1_out), .we(in_2), .clk(clock_1_out), .din(data_in), .dout(data_out));
  Clock clock_1 (.out(clock_1_out));
endmodule

module ROMu (
  input  [15:0] in_1,
  output [31:0] out_2
);
endmodule
